// Logisim project surprice.circ as structural Verilog: 6 circuits, main circuit main
module main (
);

  wire alu_1_out_5;
  wire [31:0] alu_1_y;

  ALU alu_1 (.F(3'b101), .B(32'h1), .A(32'h1), .Y(alu_1_y), .out_5(alu_1_out_5));
  Hex_Digit_Display hex_digit_display_1 (.value(alu_1_y[31:28]));  // open: dp
  LED led_1 (.in(alu_1_out_5));
  Hex_Digit_Display hex_digit_display_2 (.value(alu_1_y[23:20]));  // open: dp
  Hex_Digit_Display hex_digit_display_3 (.value(alu_1_y[27:24]));  // open: dp
  Hex_Digit_Display hex_digit_display_4 (.value(alu_1_y[19:16]));  // open: dp
  Hex_Digit_Display hex_digit_display_5 (.value(alu_1_y[15:12]));  // open: dp
  Hex_Digit_Display hex_digit_display_6 (.value(alu_1_y[11:8]));  // open: dp
  Hex_Digit_Display hex_digit_display_7 (.value(alu_1_y[3:0]));  // open: dp
  Hex_Digit_Display hex_digit_display_8 (.value(alu_1_y[7:4]));  // open: dp
endmodule

module ALU (
  input  [2:0] F,
  input  [31:0] B,
  input  [31:0] A,
  output [31:0] Y,
  output out_5
);

  wire bitselector_1_out;
  wire [31:0] adder_1_out, and_1_out, bit_extender_1_out, multiplexer_1_out, multiplexer_3_out,
       multiplier_1_out, not_1_out, or_1_out;

  assign not_1_out = ~B;  // NOT_Gate not_1, 32 bits wide
  Multiplexer #(.width(32)) multiplexer_1 (.in0(B), .in1(not_1_out), .out(multiplexer_1_out), .sel(F[2]));  // open: en
  assign and_1_out = multiplexer_1_out & A;  // AND_Gate and_1, 32 bits wide
  assign or_1_out = multiplexer_1_out | A;  // OR_Gate or_1, 32 bits wide
  Adder #(.width(32)) adder_1 (.a(multiplexer_1_out), .b(A), .out(adder_1_out), .cin(F[2]));  // open: cout
  BitSelector #(.width(32)) bitselector_1 (.in(adder_1_out), .out(bitselector_1_out), .sel(5'b10001));
  Multiplexer #(.select(2), .width(32)) multiplexer_2 (
    .in0(and_1_out), .in1(or_1_out), .in2(adder_1_out), .in3(multiplexer_3_out), .out(Y), .sel(F[1:0]));  // open: en
  Multiplier #(.width(32)) multiplier_1 (.a(B), .b(A), .out(multiplier_1_out));  // open: cin, cout
  assign bit_extender_1_out = {{31{1'b0}}, bitselector_1_out};  // Bit_Extender bit_extender_1
  Multiplexer #(.width(32)) multiplexer_3 (
    .in0(multiplier_1_out), .in1(bit_extender_1_out), .out(multiplexer_3_out), .sel(F[2]));  // open: en
  Comparator #(.width(32), .mode("unsigned")) comparator_1 (.a(Y), .b({32{1'b0}}), .eq(out_5));  // open: gt, lt
endmodule

module Datapath (
  output [31:0] Data_Memory,
  output [31:0] v0
);

  wire alu_1_out_5, and_1_out, clock_1_out, controlunit_1_alusrc, controlunit_1_branch, controlunit_1_regdst,
       controlunit_1_regwrite;
  wire [2:0] controlunit_1_alucontrol, multiplexer_3_out;
  wire [7:0] adder_1_out, adder_2_out, multiplexer_1_out, register_1_q, shifter_1_out, shifter_2_out;
  wire [31:0] bit_extender_1_out, multiplexer_2_out, registerfile_1_rd1, registerfile_1_rd2, rom_1_data;

  Multiplexer #(.width(8)) multiplexer_1 (
    .in0(adder_1_out), .in1(adder_2_out), .out(multiplexer_1_out), .sel(and_1_out));  // open: en
  Clock clock_1 (.out(clock_1_out));
  Register register_1 (.D(multiplexer_1_out), .Q(register_1_q), .clk(clock_1_out));  // open: en, clr
  Shifter #(.shift("lr")) shifter_1 (.in(register_1_q), .\dist (3'b010), .out(shifter_1_out));
  Adder adder_1 (.a(register_1_q), .b(8'h4), .out(adder_1_out));  // open: cin, cout
  ROM #(.dataWidth(32)) rom_1 (.addr(shifter_1_out), .data(rom_1_data));  // open: sel
  ControlUnit controlunit_1 (
    .Instruction(rom_1_data), .RegWrite(controlunit_1_regwrite), .ALUControl(controlunit_1_alucontrol),
    .ALUSrc(controlunit_1_alusrc), .Branch(controlunit_1_branch), .RegDst(controlunit_1_regdst));  // open: MemWrite, MemToReg
  RegisterFile registerfile_1 (
    .CLK(clock_1_out), .A1(rom_1_data[23:21]), .WD3(Data_Memory), .A2(rom_1_data[18:16]),
    .RD1(registerfile_1_rd1), .RD2(registerfile_1_rd2), .A3(multiplexer_3_out), .V0(v0),
    .WE3(controlunit_1_regwrite));
  Multiplexer #(.width(32), .enable("false")) multiplexer_2 (
    .in0(registerfile_1_rd2), .in1(bit_extender_1_out), .out(multiplexer_2_out), .sel(controlunit_1_alusrc));
  Multiplexer #(.width(3), .enable("false")) multiplexer_3 (
    .in0(rom_1_data[18:16]), .in1(rom_1_data[13:11]), .out(multiplexer_3_out), .sel(controlunit_1_regdst));
  ALU alu_1 (
    .F(controlunit_1_alucontrol), .B(multiplexer_2_out), .A(registerfile_1_rd1), .Y(Data_Memory),
    .out_5(alu_1_out_5));
  assign bit_extender_1_out = {{16{rom_1_data[15]}}, rom_1_data[15:0]};  // Bit_Extender bit_extender_1
  and and_1 (and_1_out, controlunit_1_branch, alu_1_out_5);
  Shifter shifter_2 (.in(bit_extender_1_out[7:0]), .\dist (3'b010), .out(shifter_2_out));
  Adder adder_2 (.a(shifter_2_out), .b(adder_1_out), .out(adder_2_out));  // open: cin, cout

  // Notes on the sheet:
  //   contents of rom_1 (hex, n*v repeats v):
  //   20040008 20020001 10800005 0 70441002 2084ffff 1000fffb 0 20
endmodule

module Tests (
  output [31:0] Y,
  output [7:0] out_2,
  output [7:0] out_3,
  output [2:0] out_4
);

  BitSelector #(.width(32), .group(8)) bitselector_1 (.in(32'h12356789), .out(out_2), .sel(2'b01));
  BitSelector #(.width(32), .group(8)) bitselector_2 (.in(32'h12356789), .out(out_3), .sel(2'b01));
  BitSelector #(.group(3)) bitselector_3 (.in(out_3), .out(out_4), .sel(2'b00));

  assign Y = 32'hf4010207;

  // Notes on the sheet:
  //   binary values in Logisim. Convince yourself how the bits are displayed.
  //   Example 2: The bit selector is configured to have 32  
  //   bit group #1 (starting at index 0) is selected for the output.
  //   That is, the 8 bits 0x67 at bit indices 15..8  are sent to the output.
  //   Example 3: Now, assume that you want to extract 3 bits at   
  //   Example 1: A simple example that illustrates how 32-bit values are displayed as 
  //   input bits and 8 output bits. The parameter constant is 1, which means that   
  //   bit indices 10..8. This can be accoplished by putting two bit selecotrs in series.
endmodule

module RegisterFile (
  input  CLK,
  input  [2:0] A1,
  input  [31:0] WD3,
  input  [2:0] A2,
  input  WE3,
  input  [2:0] A3,
  output [31:0] RD1,
  output [31:0] RD2,
  output [31:0] V0
);

  wire and_1_out, and_2_out, and_3_out, and_4_out, and_5_out, and_6_out, and_7_out, and_8_out,
       decoder_1_out0, decoder_1_out1, decoder_1_out2, decoder_1_out3, decoder_1_out4, decoder_1_out5,
       decoder_1_out6, decoder_1_out7;
  wire [31:0] register_1_q, register_3_q, register_4_q, register_5_q, register_6_q, register_7_q,
       register_8_q;

  Decoder #(.select(3)) decoder_1 (
    .out0(decoder_1_out0), .out1(decoder_1_out1), .out2(decoder_1_out2), .out3(decoder_1_out3),
    .out4(decoder_1_out4), .out5(decoder_1_out5), .out6(decoder_1_out6), .out7(decoder_1_out7), .sel(A3));  // open: en
  and and_1 (and_1_out, WE3, decoder_1_out0);
  Register #(.width(32)) register_1 (.D(WD3), .en(and_2_out), .Q(register_1_q), .clk(CLK));  // open: clr
  and and_2 (and_2_out, WE3, decoder_1_out1);
  Register #(.width(32)) register_2 (.D(WD3), .en(and_3_out), .Q(V0), .clk(CLK));  // open: clr
  and and_3 (and_3_out, WE3, decoder_1_out2);
  Register #(.width(32)) register_3 (.D(WD3), .en(and_4_out), .Q(register_3_q), .clk(CLK));  // open: clr
  and and_4 (and_4_out, WE3, decoder_1_out3);
  Register #(.width(32)) register_4 (.D(WD3), .en(and_5_out), .Q(register_4_q), .clk(CLK));  // open: clr
  and and_5 (and_5_out, WE3, decoder_1_out4);
  Register #(.width(32)) register_5 (.D(WD3), .en(and_6_out), .Q(register_5_q), .clk(CLK));  // open: clr
  and and_6 (and_6_out, WE3, decoder_1_out5);
  Register #(.width(32)) register_6 (.D(WD3), .en(and_7_out), .Q(register_6_q), .clk(CLK));  // open: clr
  and and_7 (and_7_out, WE3, decoder_1_out6);
  Register #(.width(32)) register_7 (.D(WD3), .en(and_8_out), .Q(register_7_q), .clk(CLK));  // open: clr
  and and_8 (and_8_out, WE3, decoder_1_out7);
  Register #(.width(32)) register_8 (.D({32{1'b0}}), .en(and_1_out), .Q(register_8_q), .clk(CLK));  // open: clr
  Multiplexer #(.select(3), .width(32)) multiplexer_1 (
    .in0(register_8_q), .in1(register_1_q), .in2(V0), .in3(register_3_q), .in4(register_4_q),
    .in5(register_5_q), .in6(register_6_q), .in7(register_7_q), .out(RD1), .sel(A1));  // open: en
  Multiplexer #(.select(3), .width(32)) multiplexer_2 (
    .in0(register_8_q), .in1(register_1_q), .in2(V0), .in3(register_3_q), .in4(register_4_q),
    .in5(register_5_q), .in6(register_6_q), .in7(register_7_q), .out(RD2), .sel(A2));  // open: en

  // Notes on the sheet:
  //   rd
  //   Write
  //   rs
  //   rt
  //   The adress for the source
  //   return value
  //   storing data word
endmodule

module ControlUnit (
  input  [31:0] Instruction,
  output RegDst,
  output RegWrite,
  output ALUSrc,
  output [2:0] ALUControl,
  output Branch,
  output MemWrite,
  output MemToReg
);

  wire comparator_3_eq;
  wire [2:0] multiplexer_1_out;
  wire [5:0] bitselector_1_out;
  wire [31:0] shifter_1_out;

  Shifter #(.width(32), .shift("lr")) shifter_1 (.in(Instruction), .\dist (5'b11010), .out(shifter_1_out));
  BitSelector #(.width(32), .group(6)) bitselector_1 (.in(shifter_1_out), .out(bitselector_1_out), .sel(3'b000));
  Comparator #(.width(6), .mode("unsigned")) comparator_1 (
    .a(bitselector_1_out), .b(6'b001000), .eq(ALUSrc));  // open: gt, lt
  Comparator #(.width(6), .mode("unsigned")) comparator_2 (
    .a(bitselector_1_out), .b({6{1'b0}}), .eq(RegDst));  // open: gt, lt
  Comparator #(.width(6), .mode("unsigned")) comparator_3 (
    .a(bitselector_1_out), .b(6'b011100), .eq(comparator_3_eq));  // open: gt, lt
  Comparator #(.width(6), .mode("unsigned")) comparator_4 (
    .a(bitselector_1_out), .b(6'b000100), .eq(Branch));  // open: gt, lt
  Comparator #(.width(6), .mode("unsigned")) comparator_5 (
    .a(bitselector_1_out), .b(6'b010011), .eq(MemWrite));  // open: gt, lt
  Comparator #(.width(6), .mode("unsigned")) comparator_6 (
    .a(bitselector_1_out), .b(6'b101011), .eq(MemToReg));  // open: gt, lt
  Multiplexer #(.width(3), .enable("false")) multiplexer_1 (
    .in0(3'b010), .in1(3'b110), .out(multiplexer_1_out), .sel(Branch));
  or or_1 (RegWrite, ALUSrc, RegDst);
  Multiplexer #(.width(3)) multiplexer_2 (
    .in0(multiplexer_1_out), .in1(3'b011), .out(ALUControl), .sel(comparator_3_eq));  // open: en
endmodule
